# Fritzing sketch pi_hat_circuit (saved by Fritzing 0.9.3b)

parts:
  Part1 = Adafruit Perma-Proto HAT [part_number="Adafruit #2314 and #2310"]
  Q6 = NPN-Transistor [package="TO92 [THT]"]
  R10 = Resistor [tolerance=±20% resistance=270 package=THT]
  R11 = Resistor [tolerance=±20% resistance=270 package=THT]
  R12 = Resistor [tolerance=±5% resistance=220 package=THT]
  R13 = Resistor [tolerance=±5% resistance=220 package=THT]
  Q7 = NPN-Transistor [package="TO92 [THT]"]
  R14 = Resistor [tolerance=±5% resistance=220 package=THT]
  R15 = Resistor [tolerance=±20% resistance=270 package=THT]
  Q8 = NPN-Transistor [package="TO92 [THT]"]
  C2 = Electrolytic Capacitor [capacitance=1µF package="100 mil [THT, electrolytic]"]
  D2 = Diode [package=diode-1n4148]
  Q9 = NPN-Transistor [package="TO92 [THT]"]
  LED2 = LED - 5mm [color="White (4500K)" package="5 mm [THT]"]
  R16 = Resistor [tolerance=±5% resistance=1k package=THT]
  J6 = female pin header, 2 pins [form="♀ (female)"]
  J7 = female pin header, 2 pins [form="♀ (female)"]
  J8 = female pin header, 2 pins [form="♀ (female)"]
  S6 = Square Pushbutton
  R17 = Resistor [tolerance=±20% resistance=3.9k package=THT]
  Part2 = Adafruit DC+Stepper Motor HAT [part_number="Adafruit #2348"]
  Part3 = Adafruit AT42QT1010 Standalone Momentary Capacitive Touch Sensor [part_number="Adafruit #1374"]
  Part4 = Adafruit AT42QT1010 Standalone Momentary Capacitive Touch Sensor [part_number="Adafruit #1374"]
  Part5 = Adafruit AT42QT1010 Standalone Momentary Capacitive Touch Sensor [part_number="Adafruit #1374"]
  S7 = Square Pushbutton
  J9 = female pin header, 2 pins [form="♀ (female)"]
  Pololu_A1 = Pololu A4988 [package=SO16]
  Part6 = Adafruit Perma-Proto HAT [part_number="Adafruit #2314 and #2310"]
  M1 = Stepper Motor - Bipolar
  J10 = female pin header, 2 pins [form="♀ (female)"]
  Part7 = Adafruit AT42QT1010 Standalone Momentary Capacitive Touch Sensor [part_number="Adafruit #1374"]
  Part8 = Adafruit AT42QT1010 Standalone Momentary Capacitive Touch Sensor [part_number="Adafruit #1374"]
  Part9 = Adafruit AT42QT1010 Standalone Momentary Capacitive Touch Sensor [part_number="Adafruit #1374"]
  C3 = Electrolytic Capacitor [capacitance=0.1mF package="100 mil [THT, electrolytic]"]
  J11 = female pin header, 2 pins [form="♀ (female)"]
  R18 = Resistor [tolerance=±5% resistance=1k package=THT]
  LED7 = LED - 5mm [color="White (6500K)" package="5 mm [THT]"]
  S8 = Square Pushbutton
  Pololu_A2 = Pololu A4988 [package=SO16]
  M2 = Stepper Motor - Bipolar
  J12 = female pin header, 2 pins [form="♀ (female)"]
  Part11 = Adafruit AT42QT1010 Standalone Momentary Capacitive Touch Sensor [part_number="Adafruit #1374"]
  Part12 = Adafruit AT42QT1010 Standalone Momentary Capacitive Touch Sensor [part_number="Adafruit #1374"]
  Part13 = Adafruit AT42QT1010 Standalone Momentary Capacitive Touch Sensor [part_number="Adafruit #1374"]
  C4 = Electrolytic Capacitor [capacitance=0.1mF package="100 mil [THT, electrolytic]"]
  J13 = female pin header, 2 pins [form="♀ (female)"]
  R19 = Resistor [tolerance=±5% resistance=1k package=THT]
  LED8 = LED - 5mm [color="White (6500K)" package="5 mm [THT]"]
  Part10 = Adafruit Perma-Proto HAT [part_number="Adafruit #2314 and #2310"]

nets:
  N1: Part1.GPIO4, Part1.N$61#371
  N2: Part1.GPIO18, R14.Pin_0
  N3: Part1.GPIO23, R13.Pin_0
  N4: Part1.GPIO6, R12.Pin_0
  N5: Part1.GPIO13, R17.Pin_0
  N6: Part1.GPIO20, R16.Pin_0
  N7: Part1.3.3V, Part1.N$42#276, C2.+, D2.C
  N8: Part1.GND, Part1.N$39#266, Part1.N$45#291, Part1.N$62#376, R10.Pin_0, R11.Pin_0, R15.Pin_0, C2.-
  N9: Part1.N$39#270, LED2.anode, J7.pin2
  N10: Part1.N$41, LED2.cathode, J7.pin1
  N11: Part1.N$42#280, J8.pin2
  N12: Part1.N$43#282, D2.A
  N13: Part1.N$43#283, Q9.C
  N14: Part1.N$43#285, J8.pin1
  N15: Part1.N$44#286, R17.Pin_1
  N16: Part1.N$44#288, Q9.B
  N17: Part1.N$45#293, Q9.E
  N18: Part1.N$46#296, R12.Pin_1
  N19: Part1.N$46#300, Q8.C
  N20: Part1.N$47#305, Q8.B
  N21: Part1.N$48#309, R11.Pin_1
  N22: Part1.N$48#310, Q8.E
  N23: Part1.N$55#341, R13.Pin_1
  N24: Part1.N$55#344, Q6.C
  N25: Part1.N$56#350, Q6.B
  N26: Part1.N$57#354, R10.Pin_1
  N27: Part1.N$57#355, Q6.E
  N28: Part1.N$58#356, R14.Pin_1
  N29: Part1.N$58#360, Q7.C
  N30: Part1.N$59#364, R15.Pin_1
  N31: Part1.N$59#365, Q7.E
  N32: Part1.N$60#370, Q7.B
  N33: Part1.N$61#373, J6.pin2, S6.leg1
  N34: Part1.N$62#378, J6.pin1, S6.leg0
  N35: Part2.GPIO4, Part2.N$87
  N36: Part2.GPIO17, Part2.N$82
  N37: Part2.GPIO25, Part2.N$50
  N38: Part2.GPIO12, Part2.N$13
  N39: Part2.3.3V, Part2.N$21
  N40: Part2.GND, Part2.N$8, Part2.N$45
  N41: Part2.N$10, Part4.GND
  N42: Part2.N$19, Part4.OUT
  N43: Part2.N$20, Part4.VDD
  N44: Part2.N$22, Part2.N$54
  N45: Part2.N$27, Part4.LEDA
  N46: Part2.N$44, Part3.GND
  N47: Part2.N$46, Part2.N$78
  N48: Part2.N$51, Part3.OUT
  N49: Part2.N$52, Part3.VDD
  N50: Part2.N$53, Part2.N$85
  N51: Part2.N$59, Part3.LEDA
  N52: Part2.N$73, J9.pin2
  N53: Part2.N$74, J9.pin1
  N54: Part2.N$76, Part5.GND
  N55: Part2.N$79, Part2.N$80
  N56: Part2.N$83, Part5.OUT
  N57: Part2.N$84, Part5.VDD
  N58: S7.leg0, Part6.N$61#372, J10.pin1
  N59: S7.leg1, Part6.N$62#377, J10.pin2
  N60: Pololu_A1.RESET, Pololu_A1.SLEEP
  N61: Pololu_A1.STEP, Part6.GPIO6
  N62: Pololu_A1.DIR, Part6.GPIO5
  N63: Pololu_A1.GND#8, Part6.GND, Part6.N$39#266, Part6.N$62#376
  VDD: Pololu_A1.VDD, Part6.3.3V, R18.Pin_0
  N64: Pololu_A1.1B, M1.D
  N65: Pololu_A1.1A, M1.B
  N66: Pololu_A1.2A, M1.C
  N67: Pololu_A1.2B, M1.A
  N68: Pololu_A1.GND#14, Part6.N$23#262
  N69: Pololu_A1.VMOT, Part6.N$21#251
  N70: Part6.GPIO4, Part6.N$61#371
  N71: Part6.N$1, Part9.LEDA
  N72: Part6.N$2, Part9.VDD
  N73: Part6.N$3, Part9.OUT
  N74: Part6.N$4, Part9.GND
  N75: Part6.N$9, Part7.LEDA
  N76: Part6.N$10, Part7.VDD
  N77: Part6.N$11, Part7.OUT
  N78: Part6.N$12, Part7.GND
  N79: Part6.N$21#253, C3.+
  N80: Part6.N$23#263, C3.-
  N81: Part6.N$39#269, J11.pin2, LED7.cathode
  N82: Part6.N$41#273, R18.Pin_1
  N83: Part6.N$41#274, J11.pin1, LED7.anode
  N84: Part6.N$55, Part8.LEDA
  N85: Part6.N$56, Part8.VDD
  N86: Part6.N$57, Part8.OUT
  N87: Part6.N$58, Part8.GND
  N88: S8.leg0, J12.pin1, Part10.N$61
  N89: S8.leg1, J12.pin2, Part10.N$62
  N90: Pololu_A2.ENABLE, Part10.N$39#269
  N91: Pololu_A2.MS1, Part10.N$41#274
  N92: Pololu_A2.MS2, Part10.N$42#279
  N93: Pololu_A2.MS3, Part10.N$43#284
  N94: Pololu_A2.RESET, Part10.N$44#289
  N95: Pololu_A2.SLEEP, Part10.N$45#294
  N96: Pololu_A2.STEP, Part10.N$46#299
  N97: Pololu_A2.DIR, Part10.N$47#304
  N98: Pololu_A2.GND#8, R19.Pin_0, Part10.GND
  N99: Pololu_A2.VDD, Part10.N$18#239
  N100: Pololu_A2.1B, Part10.N$17#234
  N101: Pololu_A2.1A, Part10.N$19#244
  N102: Pololu_A2.2A, Part10.N$20#249
  N103: Pololu_A2.2B, Part10.N$22#259
  N104: Pololu_A2.GND#14, Part10.N$21#254
  N105: Pololu_A2.VMOT, Part10.N$23#265
  N106: M2.A, Part10.N$22#256
  N107: M2.C, Part10.N$20#246
  N108: M2.B, Part10.N$19#241
  N109: M2.D, Part10.N$17#231
  N110: Part11.VDD, Part10.N$1
  N111: Part11.OUT, Part10.N$2
  N112: Part11.GND, Part10.N$3
  N113: Part12.LEDA, Part10.N$7#189
  N114: Part12.VDD, Part10.N$8#194
  N115: Part12.OUT, Part10.N$6
  N116: Part12.GND, Part10.N$5
  N117: Part13.LEDA, Part10.N$8#191
  N118: Part13.VDD, Part10.N$7#186
  N119: Part13.OUT, Part10.N$9
  N120: Part13.GND, Part10.N$10
  N121: C4.-, Part10.N$21#253
  N122: C4.+, Part10.N$23#263
  N123: J13.pin1, LED8.cathode, Part10.N$50#320
  N124: J13.pin2, LED8.anode, Part10.N$48#310
  N125: R19.Pin_1, Part10.N$50#319
  N126: Part10.GPIO5, Part10.N$48#306
  N127: Part10.GPIO6, Part10.N$47#301
  N128: Part10.GPIO12, Part10.N$46#296
  N129: Part10.GPIO16, Part10.N$43#281
  N130: Part10.GPIO19, Part10.N$42#276
  N131: Part10.GPIO20, Part10.N$41#271
  N132: Part10.GPIO21, Part10.N$39#266
  N133: Part10.3.3V, Part10.N$18#237
  N134: Part10.N$44#287, Part10.N$45#292

notes:
  paw rest touch sensors
  12V DC power

custom parts:
  Adafruit Perma-Proto HAT: To kick off the Adafruit HAT party, we have this Perma-Proto inspired plug in daughter board. It has a grid of 0.1" prototyping soldering holes for attaching chips, resistors, LED, potentiometers and more. The holes are connected underneath with traces to mimic the solderless breadboards you're familiar. There's also long power strips for +3V, +5V and Ground connections to the Pi. Near the top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
  Adafruit DC+Stepper Motor HAT: Let your robotic dreams come true with the new DC+Stepper Motor HAT from Adafruit. This Raspberry Pi add-on is perfect for any motion project as it can drive up to 4 DC or 2 Stepper motors with full PWM speed control. Since the Raspberry Pi does not have a lot of PWM pins, we use a fully-dedicated PWM driver chip onboard to both control motor direction and speed. This chip handles all the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
  Adafruit AT42QT1010 Standalone Momentary Capacitive Touch Sensor: This breakout board is the simplest way to create a project with a single "momentary" capacitive touch sensor. No microcontroller is required here - just power with 1.8 to 5.5VDC and touch the pad to activate the sensor. When a capacitive load is detected (e.g. a person touches the sensor-pad area) the red LED lights up and the output pin goes high. You can also solder a wire to the middle pad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
