# Fritzing sketch pi_hat_circuit (saved by Fritzing 0.9.2b)
stripboards: 4

parts:
  Part1 = Adafruit Perma-Proto HAT [part_number="Adafruit #2314 and #2310"]
  Q6 = NPN-Transistor [package="TO92 [THT]"]
  R10 = Resistor [tolerance=±20% resistance=270 package=THT]
  R11 = Resistor [tolerance=±20% resistance=270 package=THT]
  R12 = Resistor [tolerance=±5% resistance=220 package=THT]
  R13 = Resistor [tolerance=±5% resistance=220 package=THT]
  Q7 = NPN-Transistor [package="TO92 [THT]"]
  R14 = Resistor [tolerance=±5% resistance=220 package=THT]
  R15 = Resistor [tolerance=±20% resistance=270 package=THT]
  Q8 = NPN-Transistor [package="TO92 [THT]"]
  C2 = Electrolytic Capacitor [capacitance=1µF package="100 mil [THT, electrolytic]"]
  D2 = Diode [package=diode-1n4148]
  Q9 = NPN-Transistor [package="TO92 [THT]"]
  LED2 = LED - 5mm [color="White (4500K)" package="5 mm [THT]"]
  R16 = Resistor [tolerance=±5% resistance=1k package=THT]
  J6 = female pin header, 2 pins [form="♀ (female)"]
  J7 = female pin header, 2 pins [form="♀ (female)"]
  J8 = female pin header, 2 pins [form="♀ (female)"]
  S6 = Square Pushbutton
  R17 = Resistor [tolerance=±20% resistance=3.9k package=THT]
  S7 = Square Pushbutton
  J9 = female pin header, 2 pins [form="♀ (female)"]  # not connected
  Pololu_A1 = Pololu A4988 [package=SO16]
  Part6 = Adafruit Perma-Proto HAT [part_number="Adafruit #2314 and #2310"]
  M1 = Stepper Motor - Bipolar
  J10 = female pin header, 2 pins [form="♀ (female)"]
  C3 = Electrolytic Capacitor [capacitance=0.1mF package="100 mil [THT, electrolytic]"]
  J11 = female pin header, 2 pins [form="♀ (female)"]
  R18 = Resistor [tolerance=±5% resistance=1k package=THT]
  LED7 = LED - 5mm [color="White (6500K)" package="5 mm [THT]"]
  S8 = Square Pushbutton
  Pololu_A2 = Pololu A4988 [package=SO16]
  M2 = Stepper Motor - Bipolar
  J12 = female pin header, 2 pins [form="♀ (female)"]
  C4 = Electrolytic Capacitor [capacitance=0.1mF package="100 mil [THT, electrolytic]"]
  J13 = female pin header, 2 pins [form="♀ (female)"]
  R19 = Resistor [tolerance=±5% resistance=1k package=THT]
  LED8 = LED - 5mm [color="White (6500K)" package="5 mm [THT]"]
  Part10 = Adafruit Perma-Proto HAT [part_number="Adafruit #2314 and #2310"]
  Q11 = NPN-Transistor [package="TO92 [THT]"]
  R21 = Resistor [tolerance=±20% resistance=3.9k package=THT]
  J15 = female pin header, 2 pins [form="♀ (female)"]  # not connected
  D4 = Diode [package=diode-1n4148]
  C5 = Electrolytic Capacitor [capacitance=1µF package="100 mil [THT, electrolytic]"]  # not connected
  J16 = female pin header, 3 pins [form="♀ (female)"]
  J17 = female pin header, 2 pins [form="♀ (female)"]

nets:
  N1: Part1.GPIO4, Part1.N$61#371
  N2: Part1.GPIO18, R14.Pin_0
  N3: Part1.GPIO23, R13.Pin_0
  N4: Part1.GPIO6, R12.Pin_0
  N5: Part1.GPIO13, R17.Pin_0
  N6: Part1.GPIO20, R16.Pin_0
  N7: Part1.GND, Part1.N$39#266, Part1.N$45#291, Part1.N$62#376, R10.Pin_0, R11.Pin_0, R15.Pin_0, C2.-
  N8: Part1.3.3V, Part1.N$42#276, C2.+, D2.C
  N9: Part1.N$39#270, LED2.anode, J7.pin2
  N10: Part1.N$41, LED2.cathode, J7.pin1
  N11: Part1.N$42#280, J8.pin2
  N12: Part1.N$43#282, D2.A
  N13: Part1.N$43#283, Q9.C
  N14: Part1.N$43#285, J8.pin1
  N15: Part1.N$44#286, R17.Pin_1
  N16: Part1.N$44#288, Q9.B
  N17: Part1.N$45#293, Q9.E
  N18: Part1.N$46#296, R12.Pin_1
  N19: Part1.N$46#300, Q8.C
  N20: Part1.N$47#305, Q8.B
  N21: Part1.N$48#309, R11.Pin_1
  N22: Part1.N$48#310, Q8.E
  N23: Part1.N$55#341, R13.Pin_1
  N24: Part1.N$55#344, Q6.C
  N25: Part1.N$56#350, Q6.B
  N26: Part1.N$57#354, R10.Pin_1
  N27: Part1.N$57#355, Q6.E
  N28: Part1.N$58#356, R14.Pin_1
  N29: Part1.N$58#360, Q7.C
  N30: Part1.N$59#364, R15.Pin_1
  N31: Part1.N$59#365, Q7.E
  N32: Part1.N$60#370, Q7.B
  N33: Part1.N$61#373, J6.pin2, S6.leg1
  N34: Part1.N$62#378, J6.pin1, S6.leg0
  N35: S7.leg0, Part6.N$61#372, J10.pin1
  N36: S7.leg1, Part6.N$62#377, J10.pin2
  N37: Pololu_A1.RESET, Pololu_A1.SLEEP
  N38: Pololu_A1.STEP, Part6.GPIO6
  N39: Pololu_A1.DIR, Part6.GPIO5
  N40: Pololu_A1.GND#8, Part6.GND, Part6.N$39#266, Part6.N$62#376
  VDD: Pololu_A1.VDD, Part6.3.3V, R18.Pin_0
  N41: Pololu_A1.1B, M1.D
  N42: Pololu_A1.1A, M1.B
  N43: Pololu_A1.2A, M1.C
  N44: Pololu_A1.2B, M1.A
  N45: Pololu_A1.GND#14, Part6.N$23#262
  N46: Pololu_A1.VMOT, Part6.N$21#251
  N47: Part6.GPIO4, Part6.N$61#371
  N48: Part6.N$21#253, C3.+
  N49: Part6.N$23#263, C3.-
  N50: Part6.N$39#269, J11.pin2, LED7.cathode
  N51: Part6.N$41#273, R18.Pin_1
  N52: Part6.N$41#274, J11.pin1, LED7.anode
  N53: S8.leg0, J12.pin1, Part10.N$61#375
  N54: S8.leg1, J12.pin2, Part10.N$62#380
  N55: Pololu_A2.ENABLE, Part10.N$39#269
  N56: Pololu_A2.MS1, Part10.N$41#274
  N57: Pololu_A2.MS2, Part10.N$42#279
  N58: Pololu_A2.MS3, Part10.N$43#284
  N59: Pololu_A2.RESET, Part10.N$44#289
  N60: Pololu_A2.SLEEP, Part10.N$45#294
  N61: Pololu_A2.STEP, Part10.N$46#299
  N62: Pololu_A2.DIR, Part10.N$47#304
  N63: Pololu_A2.GND#8, R19.Pin_0, Part10.GND, Part10.N$62#376, J16.pin2, J17.pin1
  N64: Pololu_A2.VDD, Part10.N$18#239
  N65: Pololu_A2.1B, Part10.N$17#234
  N66: Pololu_A2.1A, Part10.N$19#244
  N67: Pololu_A2.2A, Part10.N$20#249
  N68: Pololu_A2.2B, Part10.N$22#259
  N69: Pololu_A2.GND#14, Part10.N$21#254
  N70: Pololu_A2.VMOT, Part10.N$23#265
  N71: M2.A, Part10.N$22#256
  N72: M2.C, Part10.N$20#246
  N73: M2.B, Part10.N$19#241
  N74: M2.D, Part10.N$17#231
  N75: C4.-, Part10.N$21#253
  N76: C4.+, Part10.N$23#263
  N77: J13.pin1, LED8.cathode, Part10.N$50#320
  N78: J13.pin2, LED8.anode, Part10.N$48#310
  N79: R19.Pin_1, Part10.N$50#319
  N80: Part10.GPIO17, Part10.N$61#371
  N81: Part10.GPIO25, Part10.N$49#312
  N82: Part10.GPIO5, Part10.N$48#306
  N83: Part10.GPIO6, Part10.N$47#301
  N84: Part10.GPIO12, Part10.N$46#296
  N85: Part10.GPIO16, Part10.N$43#281
  N86: Part10.GPIO19, Part10.N$42#276
  N87: Part10.GPIO20, Part10.N$41#271
  N88: Part10.GPIO21, Part10.N$39#266
  N89: Part10.3.3V, Part10.N$18#237, J16.pin3, J17.pin2
  N90: Part10.N$44#287, Part10.N$45#292
  N91: Part10.N$49#311, J16.pin1
  N92: Q11.B, R21.Pin_1
  N93: Q11.C, D4.A

notes:
  paw rest touch sensors
  12V DC power

custom parts:
  Adafruit Perma-Proto HAT: To kick off the Adafruit HAT party, we have this Perma-Proto inspired plug in daughter board. It has a grid of 0.1" prototyping soldering holes for attaching chips, resistors, LED, potentiometers and more. The holes are connected underneath with traces to mimic the solderless breadboards you're familiar. There's also long power strips for +3V, +5V and Ground connections to the Pi. Near the top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
