# Fritzing sketch pi_hat_circuit (saved by Fritzing 0.9.3b)

parts:
  C2 = Electrolytic Capacitor [capacitance=1µF package="100 mil [THT, electrolytic]"]  # not connected
  D2 = Diode [package=diode-1n4148]
  Q9 = NPN-Transistor [package="TO92 [THT]"]
  LED2 = LED - 5mm [color="White (4500K)" package="5 mm [THT]"]
  R16 = Resistor [tolerance=±5% resistance=1k package=THT]
  J8 = female pin header, 2 pins [form="♀ (female)"]  # not connected
  S6 = Square Pushbutton
  R17 = Resistor [tolerance=±20% resistance=3.9k package=THT]
  J9 = female pin header, 1 pin [form="♀ (female)"]  # not connected
  IC1 = DIP - 8 pins [chip_label=IC package="DIP (Dual Inline) [THT]"]
  J12 = female pin header, 1 pin [form="♀ (female)"]  # not connected
  Q10 = NPN-Transistor [package="TO92 [THT]"]
  D3 = Diode [package=diode-1n4148]
  R18 = Resistor [tolerance=±20% resistance=3.9k package=THT]
  J13 = female pin header, 2 pins [form="♀ (female)"]
  J14 = female pin header, 2 pins [form="♀ (female)"]
  S7 = Square Pushbutton
  LED3 = LED - 5mm [color="White (4500K)" package="5 mm [THT]"]
  J15 = female pin header, 2 pins [form="♀ (female)"]  # not connected
  J16 = female pin header, 2 pins [form="♀ (female)"]
  J17 = female pin header, 2 pins [form="♀ (female)"]
  Part1 = Reed Relay
  Q11 = NPN-Transistor [package="TO92 [THT]"]
  J18 = female pin header, 4 pins [form="♀ (female)"]  # not connected

nets:
  N1: D2.C, Q10.C
  N2: Q9.B, R18.Pin_0
  N3: Q9.C, D3.C
  N4: LED2.cathode, J17.pin2
  N5: LED2.anode, R16.Pin_0, LED3.anode, J17.pin1
  N6: S6.leg0, S7.leg1
  N7: S6.leg1, IC1.pin3, J14.pin2
  N8: R17.Pin_0, Q10.B
  N9: R17.Pin_1, IC1.pin4
  N10: IC1.pin_9, R18.Pin_1
  N11: IC1.pin_22, J13.pin2, S7.leg0
  N12: IC1.pin_30, J13.pin1
  N13: IC1.pin_31, J14.pin1
  N14: LED3.cathode, J16.pin2
  N15: Part1.A2, Q11.E

custom parts:
  DIP - 8 pins: A DIP stand-in part for whatever IC you want. With 8 pins on a 300mil dual inline package (DIP) footprint.
  Reed Relay: 9007-05-01 - Reed Relay, SPST-NO, 5 VDC, Spartan 9007 Series, Through Hole, 500 ohm, 500 mA
